# Fritzing sketch notifheure-reveil (saved by Fritzing 0.9.3b)
circuit board: 23.6298cm x 13.508cm
breadboards: 1
stripboards: 2

parts:
  WeMos_D1_Mini2 = WeMos D1 Mini
  S1 = Momentary Switch [package=ksa_sealed_tac_switch]
  S2 = Momentary Switch [package=ksa_sealed_tac_switch]
  R1 = Resistor [tolerance=±5% resistance=220 package=THT]
  R2 = Resistor [tolerance=±5% resistance=220 package=THT]
  LED2 = LED - 5mm [color="Red (633nm)" package="5 mm [THT]"]
  RHT1 = Humidity and Temperature Sensor RHT03
  R3 = PHOTOCELL [package=photocell]
  Composant1 = LED Matrix - Serial Interface - Red/Green/Blue
  RHT2 = Humidity and Temperature Sensor RHT03
  S3 = Momentary Switch [package=ksa_sealed_tac_switch]
  S4 = Momentary Switch [package=ksa_sealed_tac_switch]
  LED3 = LED - 5mm [color="Red (633nm)" package="5 mm [THT]"]
  R4 = Resistor [tolerance=±5% resistance=220 package=THT]
  R5 = PHOTOCELL [package=photocell]
  R6 = Resistor [tolerance=±5% resistance=220 package=THT]
  Composant2 = LED Matrix - Serial Interface - Red/Green/Blue  # not connected
  J1 = Piezo Speaker
  J2 = Piezo Speaker  # not connected

nets:
  N1: WeMos_D1_Mini2.3V3, RHT1.Data-signal, RHT1.GND_1, R3.P$1
  N2: WeMos_D1_Mini2.5V, Composant1.MOSI
  N3: WeMos_D1_Mini2.A0, R2.Pin_0, R3.P$2
  N4: WeMos_D1_Mini2.D0, RHT1.Vcc
  N5: WeMos_D1_Mini2.D1, R1.Pin_1
  N6: WeMos_D1_Mini2.D2, J1.pin2
  N7: WeMos_D1_Mini2.D3, S2.4
  N8: WeMos_D1_Mini2.D4, S1.4
  N9: WeMos_D1_Mini2.D5, WeMos_D1_Mini2.D6, Composant1.VCC
  N10: WeMos_D1_Mini2.D7, Composant1.SCK
  N11: WeMos_D1_Mini2.G, S1.2, S2.2, R2.Pin_1, LED2.cathode, Composant1.CS, J1.pin1
  N12: R1.Pin_0, LED2.anode
  N13: RHT2.Vcc, RHT2.GND_2, S3.2, S4.2, LED3.cathode, R5.P$1, R6.Pin_1
  N14: LED3.anode, R4.Pin_0
  N15: R5.P$2, R6.Pin_0

notes:
  G
  3V3
  A0
  D0
  D3
  D4
  D1
  VCC
  GND
  DIN
  CS
  CLK
  5V
  D7
  D6
  D5
  D2
